# Fritzing sketch 02.自动浇水实验 (saved by Fritzing 0.9.2b)

parts:
  KY-1 = Keyes Relay [package=THT]
  LED1 = smd LED [color="Green (555nm)" package="1206 [SMD]"]
  元件1 = TPYBoard v102
  DHT1 = DHT11 Humitidy and Temperature Sensor

nets:
  N1: KY-1.signal, 元件1.3V3#180
  N2: KY-1.power, 元件1.GND#34
  N3: KY-1.ground, 元件1.X11
  N4: KY-1.C, LED1.cathode
  N5: KY-1.NO, 元件1.GND#33
  N6: LED1.anode, 元件1.3V3#30
  N7: 元件1.Y10, DHT1.DATA
  N8: 元件1.3V3#165, DHT1.VDD
  N9: 元件1.GND#171, DHT1.NULL

custom parts:
  Keyes Relay: The Keyes 5V relay module is suitable for SCM development, home appliance control. It uses a 5V~12V TIL control signal which can control DC / AC signal.
  DHT11 Humitidy and Temperature Sensor: DHT11 Humidity and Temperature Sensor
